// Logisim project Saper.circ as structural Verilog: 1 circuit, main circuit main
module main (
  input  [30:0] in_1
);

  wire clock_1_out, clock_2_out, clock_3_out, clock_4_out, clock_5_out, clock_6_out, clock_7_out, Enter,
       Koniec, M, Reset, Start_t;
  wire [1:0] DISP;
  wire [2:0] W1D, W2D, W3D, W4D;
  wire [3:0] W1U, W2U, W3U, W4U;
  wire [4:0] counter_1_q, counter_2_q, counter_3_q, counter_4_q, counter_5_q, X5, Y5;
  wire [6:0] Klawiatura;
  wire [24:0] S_25b;
  wire [30:0] shifter_1_out, shifter_2_out, shifter_3_out, shifter_4_out, shifter_5_out;

  Clock #(.highDuration(3), .lowDuration(3)) clock_1 (.out(clock_1_out));
  Clock #(.highDuration(9), .lowDuration(9)) clock_2 (.out(clock_2_out));
  Clock #(.highDuration(2), .lowDuration(2)) clock_3 (.out(clock_3_out));
  Clock #(.highDuration(7), .lowDuration(7)) clock_4 (.out(clock_4_out));
  Clock #(.highDuration(5), .lowDuration(5)) clock_5 (.out(clock_5_out));
  Counter #(.width(5), .max('h1f)) counter_1 (.Q(counter_1_q), .clk(clock_1_out));  // open: load, D, count, carry, clr
  Counter #(.width(5), .max('h1f)) counter_2 (.Q(counter_2_q), .clk(clock_2_out));  // open: load, D, count, carry, clr
  Counter #(.width(5), .max('h1f)) counter_3 (.Q(counter_3_q), .clk(clock_3_out));  // open: load, D, count, carry, clr
  Counter #(.width(5), .max('h1f)) counter_4 (.Q(counter_4_q), .clk(clock_4_out));  // open: load, D, count, carry, clr
  Counter #(.width(5), .max('h1f)) counter_5 (.Q(counter_5_q), .clk(clock_5_out));  // open: load, D, count, carry, clr
  Button button_1 (.out(Start_t));
  Button button_2 (.out(Reset));
  DotMatrix #(.inputtype("row"), .matrixcols(31), .matrixrows(31)) dotmatrix_1 (
    .row0(shifter_1_out), .row1(shifter_2_out), .row2(shifter_3_out), .row3(shifter_4_out),
    .row4(shifter_5_out), .row5(shifter_1_out), .row6(shifter_2_out), .row7(shifter_5_out),
    .row8(shifter_3_out), .row9(shifter_2_out), .row10(shifter_4_out), .row11(shifter_5_out),
    .row12(shifter_1_out), .row13(shifter_5_out), .row14(shifter_3_out), .row15(shifter_2_out),
    .row16(shifter_5_out), .row17(shifter_3_out), .row18(shifter_4_out), .row19(shifter_5_out),
    .row20(shifter_1_out), .row21(shifter_2_out), .row22(shifter_3_out), .row23(shifter_4_out),
    .row24(shifter_5_out), .row25(shifter_1_out), .row26(shifter_2_out), .row27(shifter_5_out),
    .row28(shifter_4_out), .row29(shifter_3_out), .row30(shifter_1_out));
  Shifter #(.width(31), .shift("rr")) shifter_1 (.in(in_1), .\dist (counter_1_q), .out(shifter_1_out));
  Shifter #(.width(31), .shift("rr")) shifter_2 (.in(in_1), .\dist (counter_2_q), .out(shifter_2_out));
  Shifter #(.width(31), .shift("rr")) shifter_3 (.in(in_1), .\dist (counter_3_q), .out(shifter_3_out));
  Shifter #(.width(31), .shift("rr")) shifter_4 (.in(in_1), .\dist (counter_4_q), .out(shifter_4_out));
  Shifter #(.width(31), .shift("rr")) shifter_5 (.in(in_1), .\dist (counter_5_q), .out(shifter_5_out));
  Keyboard keyboard_1 (.clk(clock_6_out), .data(Klawiatura));  // open: re, clr, avail
  Clock clock_6 (.out(clock_6_out));
  \Sterowanie_dużo  \sterowanie_dużo_1  (
    .Wejscie_Klawiatury(Klawiatura), .Nr_Zaznaczonego_pola(S_25b), .Enter(Enter), .M(M), .X(X5), .Y(Y5));
  Clock #(.highDuration(32), .lowDuration(32)) clock_7 (.out(clock_7_out));
  licznik_czasu_main main_1 (.CLK(clock_7_out), .Stop(Koniec), .Start(Start_t), .out_5(DISP));  // open: Czas
  _7_Segment_Display u_7_segment_display_1 (
    .g(W4U[3]), .f(W4U[2]), .a(W4U[1]), .b(W4U[0]), .e(W4D[2]), .d(W4D[1]), .c(W4D[0]));  // open: dp
  _7_Segment_Display u_7_segment_display_2 (
    .g(W3U[3]), .f(W3U[2]), .a(W3U[1]), .b(W3U[0]), .e(W3D[2]), .d(W3D[1]), .c(W3D[0]));  // open: dp
  LED led_1 (.in(1'b1));
  LED led_2 (.in(1'b1));
  _7_Segment_Display u_7_segment_display_3 (
    .g(W1U[3]), .f(W1U[2]), .a(W1U[1]), .b(W1U[0]), .e(W1D[2]), .d(W1D[1]), .c(W1D[0]));  // open: dp
  _7_Segment_Display u_7_segment_display_4 (
    .g(W2U[3]), .f(W2U[2]), .a(W2U[1]), .b(W2U[0]), .e(W2D[2]), .d(W2D[1]), .c(W2D[0]));  // open: dp
  wyswietlacz_czasu wyswietlacz_czasu_1 (
    .DISP_IN__1bit_reset_0bit_clk(DISP), .O3D(W4D), .O2D(W3D), .O1D(W2D), .O0D(W1D), .O3U(W4U), .O2U(W3U),
    .O1U(W2U), .O0U(W1U));
endmodule
